# Fritzing sketch arduino_on_jeccbot_mini (saved by Fritzing 0.9.3b)

parts:
  Part1 = Arduino Mega 2560 (Rev3)
  Part2 = Adafruit Ultimate GPS v3 [part_number="Adafruit #746"]
  Part3 = 9-DOF Absolute Orientation IMU Fusion Breakout - BNO055
  Part4 = Arduino Motor Shield (Rev3)
  M1 = DC Motor
  M2 = DC Motor
  U1 = SWITCH-SPST-2 [package=switch-spst-vertical]
  S1 = SWITCH-DPDT [package=ayz0202]
  BAT1 = BC9VPC [package=bc9vpc]

nets:
  N1: Part1.D19/RX1, Part2.TX
  N2: Part1.D18/TX1, Part2.RX
  GND: Part1.GND, Part2.GND, Part3.GND, Part4.GND, BAT1.V-
  3V3: Part1.3V3, Part4.3V3
  5V: Part1.5V, Part2.VIN, Part3.5.0V, Part4.5V
  VIN: Part1.VIN, Part4.VIN
  N3: Part3.SDA_5V, Part4.SDA
  N4: Part3.SCL_5V, Part4.SCL
  N5: Part4.B-, S1.5
  N6: Part4.B+, M1.pin_1
  N7: Part4.A-, S1.2
  N8: Part4.A+, M2.pin_1
  N9: Part4.VMOT, U1.O
  N10: M1.pin_2, S1.6
  N11: M2.pin_2, S1.3
  N12: U1.P, BAT1.V+

notes:
  emergency switch

custom parts:
  Adafruit Ultimate GPS v3: We carry a few different GPS modules here in the Adafruit shop, but none that satisfied our every desire - that's why we designed this little GPS breakout board. We believe this is the Ultimate GPS module, so we named it that. It's got everything you want and more: -165 dBm sensitivity, 10 Hz updates, 66 channels 5V friendly design and only 20mA current draw Breadboard friendly + two mounting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
  9-DOF Absolute Orientation IMU Fusion Breakout - BNO055: A MEMS accelerometer, magnetometer and gyroscope on a single die with a high speed ARM Cortex-M0 based processor to digest all the sensor data, abstract the sensor fusion and real time requirements away, and spit out data you can use in quaternions, Euler angles or vectors.
